// Logisim project unidade_de_execucao.circ as structural Verilog: 1 circuit, main circuit main
module main (
);

  wire and_1_out, and_2_out, clock_1_out, not_1_out;
  wire [2:0] counter_1_q;
  wire [7:0] adder_1_out, multiplexer_1_out, multiplexer_2_out, register_1_q, register_2_q;
  wire [11:0] rom_1_data;

  Clock clock_1 (.out(clock_1_out));
  Counter #(.width(3), .max('h7)) counter_1 (.Q(counter_1_q), .clk(clock_1_out));  // open: load, D, count, carry, clr
  not not_1 (not_1_out, clock_1_out);
  ROM #(.addrWidth(3), .dataWidth(12)) rom_1 (.addr(counter_1_q), .data(rom_1_data));  // open: sel
  and and_1 (and_1_out, rom_1_data[9], not_1_out);
  and and_2 (and_2_out, rom_1_data[8], not_1_out);
  LED led_1 (.in(register_1_q[7]));
  LED led_2 (.in(register_1_q[6]));
  LED led_3 (.in(register_1_q[5]));
  LED led_4 (.in(register_1_q[1]));
  LED led_5 (.in(register_1_q[4]));
  LED led_6 (.in(register_1_q[3]));
  LED led_7 (.in(register_1_q[2]));
  Register register_1 (.D(adder_1_out), .Q(register_1_q), .clk(and_1_out));  // open: en, clr
  Register register_2 (.D(adder_1_out), .Q(register_2_q), .clk(and_2_out));  // open: en, clr
  LED led_8 (.in(register_2_q[7]));
  LED led_9 (.in(register_1_q[0]));
  LED led_10 (.in(register_2_q[6]));
  LED led_11 (.in(register_2_q[5]));
  LED led_12 (.in(register_2_q[3]));
  LED led_13 (.in(register_2_q[4]));
  LED led_14 (.in(register_2_q[0]));
  LED led_15 (.in(register_2_q[2]));
  LED led_16 (.in(register_2_q[1]));
  Multiplexer #(.width(8)) multiplexer_1 (
    .in0(rom_1_data[7:0]), .in1(register_1_q), .out(multiplexer_1_out), .sel(rom_1_data[10]));  // open: en
  Multiplexer #(.width(8)) multiplexer_2 (
    .in0({8{1'b0}}), .in1(register_2_q), .out(multiplexer_2_out), .sel(rom_1_data[11]));  // open: en
  Adder adder_1 (.a(multiplexer_1_out), .b(multiplexer_2_out), .out(adder_1_out), .cin(1'b0));  // open: cout

  // Notes on the sheet:
  //   contents of rom_1 (hex, n*v repeats v):
  //   108 208 d00 2fe d00 205 d00 300
endmodule
